# Fritzing sketch DHT11 ESP8266v12E without the base setup (saved by Fritzing 0.9.2b)

parts:
  DHT1 = DHT11 Humitidy and Temperature Sensor
  U1 = ESP8266 WiFi Module [part_number=ESP8266]
  R1 = Resistor [tolerance=±5% resistance=4.7k package=THT]

nets:
  VDD: DHT1.VDD, U1.VCC, R1.Pin_0
  N1: DHT1.DATA, U1.GPIO_5, R1.Pin_1
  GND: DHT1.GND, U1.GND

custom parts:
  DHT11 Humitidy and Temperature Sensor: DHT11 Humidity and Temperature Sensor
  ESP8266 WiFi Module: Generic WiFi Module based on the ESP8266 with onboard PCB antenna and UART communications
